// Logisim project eyadsalu.circ as structural Verilog: 10 circuits, main circuit alu
module alu (
  input  [2:0] in_1,
  input  [7:0] X,
  input  [7:0] Y,
  output [7:0] out_4,
  output SF,
  output ZF,
  output CF,
  output OF,
  output EQ
);

  wire n8bitadder_1_c__out, n8bitsubtractor_1_out_5;
  wire [7:0] n8bitadder_1_sum, n8bitarithmeticright_1_out_3, n8bitbitwiseand_1_out_3, n8bitbitwiseor_1_out_3,
       n8bitcompare_1_out_3, n8bitleftshift_1_out_3, n8bitlogicalrightshift_1_out_3, n8bitsubtractor_1_out_4;

  _8bitbitwiseor u_8bitbitwiseor_1 (.in_1(X), .in_2(Y), .out_3(n8bitbitwiseor_1_out_3));
  _8bitbitwiseAND u_8bitbitwiseand_1 (.in_1(X), .in_2(Y), .out_3(n8bitbitwiseand_1_out_3));
  _8bitadder u_8bitadder_1 (.X(X), .Y(Y), .C__in(1'b0), .C__out(n8bitadder_1_c__out), .Sum(n8bitadder_1_sum));
  _8bitsubtractor u_8bitsubtractor_1 (
    .x(X), .y(Y), .in_1(1'b0), .out_5(n8bitsubtractor_1_out_5), .out_4(n8bitsubtractor_1_out_4));  // open: out_6
  _8bitleftshift u_8bitleftshift_1 (.in_1(X), .in_2(Y), .out_3(n8bitleftshift_1_out_3));
  _8bitlogicalrightshift u_8bitlogicalrightshift_1 (.in_1(X), .in_2(Y), .out_3(n8bitlogicalrightshift_1_out_3));
  _8bitarithmeticright u_8bitarithmeticright_1 (.in_1(X), .in_2(Y), .out_3(n8bitarithmeticright_1_out_3));
  _8bitcompare u_8bitcompare_1 (.in_1(X), .in_2(Y), .out_3(n8bitcompare_1_out_3));
  Multiplexer #(.select(3), .width(8)) multiplexer_1 (
    .in0(n8bitbitwiseor_1_out_3), .in1(n8bitbitwiseand_1_out_3), .in2(n8bitadder_1_sum),
    .in3(n8bitsubtractor_1_out_4), .in4(n8bitleftshift_1_out_3), .in5(n8bitlogicalrightshift_1_out_3),
    .in6(n8bitarithmeticright_1_out_3), .in7(n8bitcompare_1_out_3), .out(out_4), .sel(in_1));  // open: en
  Comparator comparator_1 (.a(out_4), .b({8{1'b0}}), .lt(SF));  // open: gt, eq
  Comparator comparator_2 (.a(X), .b(Y), .eq(EQ));  // open: gt, lt
  and and_1 (OF, n8bitsubtractor_1_out_5, n8bitadder_1_c__out);
  Comparator comparator_3 (.a(out_4), .b({8{1'b0}}), .eq(ZF));  // open: gt, lt
  and and_2 (CF, n8bitsubtractor_1_out_5, n8bitadder_1_c__out);

  // Notes on the sheet:
  //   000 =or$001 = AND$010 = ADD$011 = SUB$100 = left shift$101 = lsr$110 = asr$111 = compare
endmodule

// ADD
module _8bitadder (
  input  C__in,
  input  [7:0] X,
  input  [7:0] Y,
  output [7:0] Sum,
  output C__out
);

  Adder adder_1 (.a(X), .b(Y), .out(Sum), .cin(C__in), .cout(C__out));
endmodule

// Subtract
module _8bitsubtractor (
  input  in_1,
  input  [7:0] x,
  input  [7:0] y,
  output [7:0] out_4,
  output out_5,
  output out_6
);

  wire [7:0] adder_1_out, not_1_out;

  assign not_1_out = ~y;  // NOT_Gate not_1, 8 bits wide
  Adder adder_1 (.a(not_1_out), .b(8'h1), .out(adder_1_out), .cin(in_1), .cout(out_6));
  Adder adder_2 (.a(x), .b(adder_1_out), .out(out_4), .cin(in_1), .cout(out_5));
endmodule

// OR
module _8bitbitwiseor (
  input  [7:0] in_1,
  input  [7:0] in_2,
  output [7:0] out_3
);

  assign out_3 = in_1 | in_2;  // OR_Gate or_1, 8 bits wide
endmodule

// AND
module _8bitbitwiseAND (
  input  [7:0] in_1,
  input  [7:0] in_2,
  output [7:0] out_3
);

  assign out_3 = in_1 & in_2;  // AND_Gate and_1, 8 bits wide
endmodule

// logical right shift
module _8bitlogicalrightshift (
  input  [7:0] in_1,
  input  [7:0] in_2,
  output [7:0] out_3
);

  Shifter #(.shift("lr")) shifter_1 (.in(in_1), .\dist (in_2[2:0]), .out(out_3));
endmodule

// arithmeticrigfht
module _8bitarithmeticright (
  input  [7:0] in_1,
  input  [7:0] in_2,
  output [7:0] out_3
);

  wire [7:7] shifter_1_out;

  Shifter #(.shift("lr")) shifter_1 (.in(in_1), .\dist (in_2[2:0]), .out({shifter_1_out[7], out_3[6:0]}));

  assign out_3[7] = in_1[7];
endmodule

// leftshift
module _8bitleftshift (
  input  [7:0] in_1,
  input  [7:0] in_2,
  output [7:0] out_3
);

  Shifter shifter_1 (.in(in_1), .\dist (in_2[2:0]), .out(out_3));
endmodule

// compare
module _8bitcompare (
  input  [7:0] in_1,
  input  [7:0] in_2,
  output [7:0] out_3
);

  Comparator comparator_1 (.a(in_1), .b(in_2), .lt(out_3[0]));  // open: gt, eq

  assign out_3[7:1] = {7{1'b0}};
endmodule

module main (
  input  [2:0] OP_Code,
  input  [7:0] X,
  input  [7:0] Y,
  output [7:0] Result,
  output SF,
  output ZF,
  output CF,
  output OF,
  output EQ
);

  alu alu_1 (.X(X), .Y(Y), .in_1(OP_Code), .SF(SF), .ZF(ZF), .CF(CF), .OF(OF), .EQ(EQ), .out_4(Result));

  // Notes on the sheet:
  //   000 =or$001 = AND$010 = ADD$011 = SUB$100 = left shift$101 = lsr$110 = asr$111 = compare
endmodule
