// Logisim project intro.circ as structural Verilog: 2 circuits, main circuit main
module main (
  input  _1___RESET,
  output out_2
);

  wire clock_1_out;
  wire [1:0] counter_1_q;

  Clock clock_1 (.out(clock_1_out));
  // Probe on counter_1_q
  Counter #(.width(2), .max('h3)) counter_1 (
    .Q(counter_1_q), .carry(_1___RESET), .down(clock_1_out));  // open: load, D, count, clk, clr, preset
  first_circuit first_circuit_1 (.Y(counter_1_q[0]), .X(counter_1_q[1]), .Result(out_2));
endmodule

module first_circuit (
  input  Y,
  input  X,
  output Result
);

  wire and_1_out, not_1_out;

  not not_1 (not_1_out, X);
  and and_1 (and_1_out, Y, X);
  or or_1 (Result, and_1_out, not_1_out);
endmodule
