// Logisim project part1.circ as structural Verilog: 4 circuits, main circuit main
module main (
  input  C___in,
  input  [3:0] X,
  input  [1:0] Y,
  output [3:0] Sum,
  output C__out
);

  wire [3:0] Sign2xt4_output;

  signext2to4 Sign2xt4 (.Input(Y), .Output(Sign2xt4_output));
  _4bitfulladder _4_bitadder (.X(X), .Y(Sign2xt4_output), .C_in(C___in), .C_out(C__out), .Sum(Sum));
endmodule

module fulladder (
  input  C_in,
  input  A,
  input  B,
  output Sum,
  output C_out
);

  wire and_1_out, and_2_out, xor_1_out;

  xor xor_1 (xor_1_out, A, B);
  and and_1 (and_1_out, C_in, xor_1_out);
  and and_2 (and_2_out, B, A);
  xor xor_2 (Sum, xor_1_out, C_in);
  or or_1 (C_out, and_1_out, and_2_out);
endmodule

module signext2to4 (
  input  [1:0] Input,
  output [3:0] Output
);


  assign Output = {{3{Input[1]}}, Input[0]};
endmodule

module _4bitfulladder (
  input  C_in,
  input  [3:0] X,
  input  [3:0] Y,
  output [3:0] Sum,
  output C_out
);

  wire fulladder_1_c_out, fulladder_2_c_out, fulladder_3_c_out;

  fulladder fulladder_1 (.A(X[0]), .B(Y[0]), .C_in(C_in), .C_out(fulladder_1_c_out), .Sum(Sum[0]));
  fulladder fulladder_2 (.A(X[1]), .B(Y[1]), .C_in(fulladder_1_c_out), .C_out(fulladder_2_c_out), .Sum(Sum[1]));
  fulladder fulladder_3 (.A(X[2]), .B(Y[2]), .C_in(fulladder_2_c_out), .C_out(fulladder_3_c_out), .Sum(Sum[2]));
  fulladder fulladder_4 (.A(X[3]), .B(Y[3]), .C_in(fulladder_3_c_out), .C_out(C_out), .Sum(Sum[3]));
endmodule
