// Logisim project solution.circ as structural Verilog: 2 circuits, main circuit main
module main (
  input  _1___Reset,
  output Output
);

  wire clock_1_out;
  wire [1:0] Counter_q;

  Clock clock_1 (.out(clock_1_out));
  Counter #(.width(2), .max('h3)) Counter (
    .Q(Counter_q), .clk(clock_1_out), .clr(_1___Reset), .down(clock_1_out));  // open: load, D, count, carry, preset
  // Probe on Counter_q
  first_circuit first_circuit (.X(Counter_q[0]), .Y(Counter_q[1]), .Result(Output));
endmodule

module first_circuit (
  input  X,
  input  Y,
  output Result
);

  wire and_1_out, not_1_out;

  not not_1 (not_1_out, X);
  and and_1 (and_1_out, X, Y);
  or or_1 (Result, not_1_out, and_1_out);
endmodule
